// Logisim project Labo2_ALU_Piemontesi_Trueb.circ as structural Verilog: 9 circuits, main circuit ALU_MAXV
module ALU_MAXV (
  input  [3:0] a_i,
  input  [3:0] b_i,
  output [3:0] c_o,
  output erreur_o
);

  wire [5:0] opcode_i_sw6;

  DipSwitch opcode_i (
    .sw1(opcode_i_sw6[5]), .sw2(opcode_i_sw6[4]), .sw3(opcode_i_sw6[3]), .sw4(opcode_i_sw6[2]),
    .sw5(opcode_i_sw6[1]), .sw6(opcode_i_sw6[0]));  // open: sw7, sw8
  ALU_Top ALU_Top_1 (.op_i(opcode_i_sw6), .a_i(a_i), .b_i(b_i), .c_o(c_o), .erreur_o(erreur_o));

  // Notes on the sheet:
  //   Attention, votre version de Logisim
  //   ne contient pas de tracker. Si vous
  //   enregistrez votre projet, toutes les
  //   informations du tracker seront
  //   définitivement effacées.
endmodule

module ALU_Top (
  input  [5:0] op_i,
  input  [3:0] a_i,
  input  [3:0] b_i,
  output [3:0] c_o,
  output erreur_o
);

  wire AddSub4Bits_1_carry_o, AddSub4Bits_1_negative_o, AddSub4Bits_1_overflow_o, AddSub4Bits_1_zero_o,
       and_1_out, Comparator4Bits_1_error, not_1_out;
  wire [3:0] AddSub4Bits_1_r_o, Comparator4Bits_1_cmp_o, Custom4Bits_1_s_o, Logical4Bits_1_f_o;

  not not_1 (not_1_out, op_i[5]);
  Logical4Bits Logical4Bits_1 (.op_i(op_i[5:4]), .a_i(a_i), .b_i(b_i), .f_o(Logical4Bits_1_f_o));
  Custom4Bits Custom4Bits_1 (.a_i(a_i), .s_o(Custom4Bits_1_s_o));
  AddSub4Bits AddSub4Bits_1 (
    .op_i(op_i[3:2]), .a_i(a_i), .b_i(b_i), .Negative_o(AddSub4Bits_1_negative_o),
    .zero_o(AddSub4Bits_1_zero_o), .r_o(AddSub4Bits_1_r_o), .carry_o(AddSub4Bits_1_carry_o),
    .overflow_o(AddSub4Bits_1_overflow_o));
  Comparator4Bits Comparator4Bits_1 (
    .op_i(op_i[2:0]), .Negative_i(AddSub4Bits_1_negative_o), .zero_i(AddSub4Bits_1_zero_o),
    .carry_i(AddSub4Bits_1_carry_o), .error(Comparator4Bits_1_error), .cmp_o(Comparator4Bits_1_cmp_o));
  and and_1 (and_1_out, op_i[4], not_1_out);
  Multiplexer #(.select(2), .width(4), .enable("false")) multiplexer_1 (
    .in0(AddSub4Bits_1_r_o), .in1(Comparator4Bits_1_cmp_o), .in2(Logical4Bits_1_f_o),
    .in3(Custom4Bits_1_s_o), .out(c_o), .sel(op_i[5:4]));
  Multiplexer #(.enable("false")) multiplexer_2 (
    .in0(AddSub4Bits_1_overflow_o), .in1(Comparator4Bits_1_error), .out(erreur_o), .sel(and_1_out));

  // Other names for the same wires on the sheet: addsub_op[1:0] = op_i[3:2]; comp_op[2:0] = op_i[2:0];
  //   logical_op[1:0] = op_i[5:4]; op_select[1:0] = op_i[5:4]

  // Notes on the sheet:
  //   Attention, votre version de Logisim
  //   ne contient pas de tracker. Si vous
  //   enregistrez votre projet, toutes les
  //   informations du tracker seront
  //   définitivement effacées.
endmodule

module AddSub4Bits (
  input  [1:0] op_i,
  input  [3:0] a_i,
  input  [3:0] b_i,
  output Negative_o,
  output zero_o,
  output [3:0] r_o,
  output carry_o,
  output overflow_o
);

  wire Add4Bits_1_c_o, and_1_out, and_2_out, and_3_out, CheckSignedOverflow_1_signed_overflow_o, not_1_out,
       not_2_out;
  wire [3:0] xor_1_out;

  xor xor_1 (xor_1_out[0], b_i[0], op_i[1]);
  xor xor_2 (xor_1_out[1], b_i[1], op_i[1]);
  xor xor_3 (xor_1_out[2], b_i[2], op_i[1]);
  xor xor_4 (xor_1_out[3], op_i[1], b_i[3]);
  Add4Bits Add4Bits_1 (.c_i(op_i[1]), .a_i(a_i), .b_i(xor_1_out), .r_o(r_o), .c_o(Add4Bits_1_c_o));
  xor xor_5 (carry_o, Add4Bits_1_c_o, op_i[1]);
  CheckSignedOverflow CheckSignedOverflow_1 (
    .msb_res_i(r_o[3]), .add_sub_i(op_i[1]), .msb_a_i(a_i[3]), .msb_b_i(b_i[3]),
    .signed_overflow_o(CheckSignedOverflow_1_signed_overflow_o));
  not not_1 (not_1_out, op_i[0]);
  and and_1 (and_1_out, not_1_out, r_o[3]);
  nor nor_1 (zero_o, r_o[0], r_o[1], r_o[2], r_o[3]);
  not not_2 (not_2_out, op_i[0]);
  and and_2 (and_2_out, op_i[0], carry_o);
  Multiplexer #(.enable("false")) multiplexer_1 (
    .in0(and_2_out), .in1(CheckSignedOverflow_1_signed_overflow_o), .out(overflow_o), .sel(not_2_out));
  or or_1 (Negative_o, and_1_out, and_3_out);
  and and_3 (and_3_out, carry_o, CheckSignedOverflow_1_signed_overflow_o);

  // Other names for the same wires on the sheet: un_signed = op_i[0]; ouput_msb = r_o[3]

  // Notes on the sheet:
  //   Attention, votre version de Logisim
  //   ne contient pas de tracker. Si vous
  //   enregistrez votre projet, toutes les
  //   informations du tracker seront
  //   définitivement effacées.
  //   1-> Sub
  //   0-> Add
  //   0 -> signed
  //   1 -> unsigned
endmodule

module Add4Bits (
  input  c_i,
  input  [3:0] a_i,
  input  [3:0] b_i,
  output [3:0] r_o,
  output c_o
);

  wire Add1Bit_1_c_o, Add1Bit_2_c_o, Add1Bit_3_c_o;

  Add1Bit Add1Bit_1 (.a_i(a_i[0]), .b_i(b_i[0]), .c_i(c_i), .r_o(r_o[0]), .c_o(Add1Bit_1_c_o));
  Add1Bit Add1Bit_2 (.a_i(a_i[1]), .b_i(b_i[1]), .c_i(Add1Bit_1_c_o), .r_o(r_o[1]), .c_o(Add1Bit_2_c_o));
  Add1Bit Add1Bit_3 (.a_i(a_i[2]), .b_i(b_i[2]), .c_i(Add1Bit_2_c_o), .r_o(r_o[2]), .c_o(Add1Bit_3_c_o));
  Add1Bit Add1Bit_4 (.a_i(a_i[3]), .b_i(b_i[3]), .c_i(Add1Bit_3_c_o), .r_o(r_o[3]), .c_o(c_o));

  // Notes on the sheet:
  //   Attention, votre version de Logisim
  //   ne contient pas de tracker. Si vous
  //   enregistrez votre projet, toutes les
  //   informations du tracker seront
  //   définitivement effacées.
endmodule

module Add1Bit (
  input  a_i,
  input  b_i,
  input  c_i,
  output r_o,
  output c_o
);

  wire and_1_out, and_2_out, and_3_out, xor_1_out;

  xor xor_1 (xor_1_out, a_i, b_i);
  and and_1 (and_1_out, a_i, b_i);
  and and_2 (and_2_out, a_i, c_i);
  and and_3 (and_3_out, b_i, c_i);
  xor xor_2 (r_o, xor_1_out, c_i);
  or or_1 (c_o, and_1_out, and_2_out, and_3_out);

  // Notes on the sheet:
  //   Attention, votre version de Logisim
  //   ne contient pas de tracker. Si vous
  //   enregistrez votre projet, toutes les
  //   informations du tracker seront
  //   définitivement effacées.
endmodule

module Comparator4Bits (
  input  [2:0] op_i,
  input  Negative_i,
  input  zero_i,
  input  carry_i,
  output error,
  output [3:0] cmp_o
);

  wire and_1_out, and_2_out, not_1_out, not_2_out, not_3_out, not_4_out, not_5_out, not_6_out;

  not not_1 (not_1_out, Negative_i);
  not not_2 (not_2_out, zero_i);
  not not_3 (not_3_out, carry_i);
  not not_4 (not_4_out, op_i[0]);
  not not_5 (not_5_out, op_i[1]);
  not not_6 (not_6_out, op_i[2]);
  Multiplexer #(.select(3), .enable("false")) multiplexer_1 (
    .in0(1'b0), .in1(not_1_out), .in2(Negative_i), .in3(not_2_out), .in4(zero_i), .in5(not_3_out),
    .in6(carry_i), .in7(1'b0), .out(cmp_o[0]), .sel(op_i));
  and and_1 (and_1_out, not_4_out, not_5_out, not_6_out);
  and and_2 (and_2_out, op_i[0], op_i[1], op_i[2]);
  or or_1 (error, and_1_out, and_2_out);

  assign cmp_o[3:1] = 3'b000;

  // Notes on the sheet:
  //   Attention, votre version de Logisim
  //   ne contient pas de tracker. Si vous
  //   enregistrez votre projet, toutes les
  //   informations du tracker seront
  //   définitivement effacées.
endmodule

module Logical4Bits (
  input  [1:0] op_i,
  input  [3:0] a_i,
  input  [3:0] b_i,
  output [3:0] f_o
);

  wire [3:0] and_1_out, nand_1_out, or_1_out, xor_1_out;

  assign and_1_out = a_i & b_i;  // AND_Gate and_1, 4 bits wide
  assign or_1_out = a_i | b_i;  // OR_Gate or_1, 4 bits wide
  assign nand_1_out = ~(a_i & b_i);  // NAND_Gate nand_1, 4 bits wide
  assign xor_1_out = a_i ^ b_i;  // XOR_Gate xor_1, 4 bits wide
  Multiplexer #(.select(2), .width(4), .enable("false")) multiplexer_1 (
    .in0(and_1_out), .in1(or_1_out), .in2(nand_1_out), .in3(xor_1_out), .out(f_o), .sel(op_i));

  // Notes on the sheet:
  //   Attention, votre version de Logisim
  //   ne contient pas de tracker. Si vous
  //   enregistrez votre projet, toutes les
  //   informations du tracker seront
  //   définitivement effacées.
endmodule

module Custom4Bits (
  input  [3:0] a_i,
  output [3:0] s_o
);

  ExactlyOne xor_1 (.out(s_o[0]), .in0(a_i[0]), .in1(a_i[1]), .in2(a_i[2]), .in3(a_i[3]));

  assign s_o[3:1] = 3'b000;

  // Notes on the sheet:
  //   Attention, votre version de Logisim
  //   ne contient pas de tracker. Si vous
  //   enregistrez votre projet, toutes les
  //   informations du tracker seront
  //   définitivement effacées.
endmodule

module CheckSignedOverflow (
  input  msb_res_i,
  input  add_sub_i,
  input  msb_a_i,
  input  msb_b_i,
  output signed_overflow_o
);

  wire and_1_out, and_2_out, and_3_out, and_4_out, not_1_out, not_2_out, not_3_out, not_4_out;

  not not_1 (not_1_out, add_sub_i);
  not not_2 (not_2_out, msb_b_i);
  not not_3 (not_3_out, msb_a_i);
  not not_4 (not_4_out, msb_res_i);
  and and_1 (and_1_out, msb_res_i, not_1_out, not_2_out, not_3_out);
  and and_2 (and_2_out, not_4_out, not_1_out, msb_b_i, msb_a_i);
  and and_3 (and_3_out, msb_res_i, msb_b_i, not_3_out, add_sub_i);
  and and_4 (and_4_out, not_4_out, msb_a_i, not_2_out, add_sub_i);
  or or_1 (signed_overflow_o, and_1_out, and_2_out, and_3_out, and_4_out);

  // Notes on the sheet:
  //   Attention, votre version de Logisim
  //   ne contient pas de tracker. Si vous
  //   enregistrez votre projet, toutes les
  //   informations du tracker seront
  //   définitivement effacées.
  //   1 si B >= 0
  //   1 si A >= 0
  //   1 si Add
  //   1 si B < 0
  //   1 si A < 0
  //   1 si res >= 0
  //   1 si B < 0
  //   1 si A >= 0
  //   1 si Sub
  //   1 si A < 0
  //   1 si B >= 0
  //   1 si Sub
  //   1 si res < 0
  //   1 si res >= 0
endmodule
